// Logisim project ALU.circ as structural Verilog: 1 circuit, main circuit alu
module alu (
  input  [3:0] A,
  input  [3:0] B,
  input  [1:0] ALUOp,
  output [3:0] C
);

  wire [3:0] add, sub, tunnel, tunnel_t;

  Adder #(.width(4)) adder_1 (.a(A), .b(B), .out(add));  // open: cin, cout
  Subtractor #(.width(4)) subtractor_1 (.a(A), .b(B), .out(sub));  // open: bin, bout
  assign tunnel = A & B;  // AND_Gate and_1, 4 bits wide
  assign tunnel_t = A | B;  // OR_Gate or_1, 4 bits wide
  Multiplexer #(.select(2), .width(4), .enable("false")) multiplexer_1 (
    .in0(add), .in1(sub), .in2(tunnel), .in3(tunnel_t), .out(C), .sel(ALUOp));
endmodule
