// Logisim project project3_old.circ as structural Verilog: 14 circuits, main circuit main
module main (
  input  Reset,
  output [31:0] out_2,
  output out_3,
  output [4:0] out_4,
  output [31:0] out_5,
  output out_6,
  output [4:0] out_7,
  output [31:0] out_8
);

  wire alu_1_zero, ALUSrc, Branch, Clk, MemtoReg, PCSrc, RegDst;
  wire [1:0] ExtOp;
  wire [3:0] ALUControl;
  wire [29:0] adder_1_out, adder_2_out, bit_extender_1_out, ifu_1_pc, multiplexer_1_out;
  wire [31:0] alu_1_result, dm_1_rd, ext_1_si, grf_1_rd1, multiplexer_3_out;

  Clock clock_1 (.out(Clk));
  Multiplexer #(.width(30), .enable("false")) multiplexer_1 (
    .in0(adder_1_out), .in1(adder_2_out), .out(multiplexer_1_out), .sel(PCSrc));
  IFU ifu_1 (.Instr(out_2), .Clk(Clk), .Reset(Reset), .PC_prime(multiplexer_1_out), .PC(ifu_1_pc));
  Adder #(.width(30)) adder_1 (.a(ifu_1_pc), .b(30'h1), .out(adder_1_out));  // open: cin, cout
  Controller controller_1 (
    .Op(out_2[31:26]), .Func(out_2[5:0]), .RegDst(RegDst), .RegWrite(out_3), .ALSrc(ALUSrc),
    .MemWrite(out_6), .MemtoReg(MemtoReg), .Branch(Branch), .ExtOp(ExtOp), .ALUControl(ALUControl));
  GRF grf_1 (
    .A1(out_2[25:21]), .A2(out_2[20:16]), .A3(out_4), .WD(out_5), .RD1(grf_1_rd1), .RD2(out_8), .clk(Clk),
    .WE(out_3), .reset(Reset));
  Multiplexer #(.width(5), .enable("false")) multiplexer_2 (
    .in0(out_2[20:16]), .in1(out_2[15:11]), .out(out_4), .sel(RegDst));
  EXT ext_1 (.Imm(out_2[15:0]), .SI(ext_1_si), .EXTOp(ExtOp));
  Multiplexer #(.width(32), .enable("false")) multiplexer_3 (
    .in0(out_8), .in1(ext_1_si), .out(multiplexer_3_out), .sel(ALUSrc));
  Bit_Extender #(.in_width(32), .out_width(30)) bit_extender_1 (.in(ext_1_si), .out(bit_extender_1_out));
  ALU alu_1 (
    .A(grf_1_rd1), .B(multiplexer_3_out), .Zero(alu_1_zero),
    .Result({alu_1_result[31:7], out_7, alu_1_result[1:0]}), .ALUOp(ALUControl));
  Adder #(.width(30)) adder_2 (.a(bit_extender_1_out), .b(adder_1_out), .out(adder_2_out));  // open: cin, cout
  and and_1 (PCSrc, Branch, alu_1_zero);
  DM dm_1 (.A(out_7), .WD(out_8), .RD(dm_1_rd), .Clk(Clk), .WE(out_6));
  Multiplexer #(.width(32), .enable("false")) multiplexer_4 (
    .in0({alu_1_result[31:7], out_7, alu_1_result[1:0]}), .in1(dm_1_rd), .out(out_5), .sel(MemtoReg));

  // Other names for the same wires on the sheet: MemAddr[4:0] = out_7; Instr[31:0] = out_2; MemData[31:0] = out_8;
  //   MemWrite = out_6; RegAddr[4:0] = out_4; RegData[31:0] = out_5; RegWrite = out_3

  // Notes on the sheet:
  //   PCPlus
endmodule

module IFU (
  input  [29:0] PC_prime,
  input  Clk,
  input  Reset,
  output [31:0] Instr,
  output [29:0] PC
);

  Register #(.width(30)) u_PC (.D(PC_prime), .Q(PC), .clk(Clk), .clr(Reset));  // open: en
  ROM #(.addrWidth(5), .dataWidth(32)) rom_1 (.addr(PC[4:0]), .data(Instr));  // open: sel

  // Notes on the sheet:
  //   contents of rom_1 (hex, n*v repeats v):
  //   340a0004 340b0000 340c0003 ad6b0000 16a5821 ad6b0000 16a5821 ad6b0000 16a5821 116c0001 3c0d0064
  //   16a5823 8d6e0000 16a5823 8d6f0000 16a5823 8d700000 11600001 36310064 365200c8
endmodule

module GRF (
  input  clk,
  input  WE,
  input  [4:0] A1,
  input  [4:0] A2,
  input  [4:0] A3,
  input  [31:0] WD,
  input  reset,
  output [31:0] RD1,
  output [31:0] RD2
);

  wire [31:0] r0, r1, r2, r3, r4, r5, r6, r7, r8, r9, r10, r11, r12, r13, r14, r15, r16, r17, r18, r19, r20,
       r21, r22, r23, r24, r25, r26, r27, r28, r29, r30, r31, w0, w1, w2, w3, w4, w5, w6, w7, w8, w9, w10,
       w11, w12, w13, w14, w15, w16, w17, w18, w19, w20, w21, w22, w23, w24, w25, w26, w27, w28, w29, w30,
       w31;

  Demultiplexer #(.select(5), .width(32), .tristate("true")) demultiplexer_1 (
    .out0(w0), .out1(w1), .out2(w2), .out3(w3), .out4(w4), .out5(w5), .out6(w6), .out7(w7), .out8(w8),
    .out9(w9), .out10(w10), .out11(w11), .out12(w12), .out13(w13), .out14(w14), .out15(w15), .out16(w16),
    .out17(w17), .out18(w18), .out19(w19), .out20(w20), .out21(w21), .out22(w22), .out23(w23), .out24(w24),
    .out25(w25), .out26(w26), .out27(w27), .out28(w28), .out29(w29), .out30(w30), .out31(w31), .in(WD),
    .sel(A3), .en(WE));
  Register #(.width(32)) _0 (.D({32{1'b0}}), .Q(r0), .clk(clk), .clr(reset));  // open: en
  Register #(.width(32)) _4 (.D(w4), .Q(r4), .clk(clk), .clr(reset));  // open: en
  Register #(.width(32)) _8 (.D(w8), .Q(r8), .clk(clk), .clr(reset));  // open: en
  Register #(.width(32)) _12 (.D(w12), .Q(r12), .clk(clk), .clr(reset));  // open: en
  Register #(.width(32)) _16 (.D(w16), .Q(r16), .clk(clk), .clr(reset));  // open: en
  Register #(.width(32)) _20 (.D(w20), .Q(r20), .clk(clk), .clr(reset));  // open: en
  Register #(.width(32)) _24 (.D(w24), .Q(r24), .clk(clk), .clr(reset));  // open: en
  Register #(.width(32)) _28 (.D(w28), .Q(r28), .clk(clk), .clr(reset));  // open: en
  Register #(.width(32)) _1 (.D(w1), .Q(r1), .clk(clk), .clr(reset));  // open: en
  Register #(.width(32)) _5 (.D(w5), .Q(r5), .clk(clk), .clr(reset));  // open: en
  Register #(.width(32)) _9 (.D(w9), .Q(r9), .clk(clk), .clr(reset));  // open: en
  Register #(.width(32)) _13 (.D(w13), .Q(r13), .clk(clk), .clr(reset));  // open: en
  Register #(.width(32)) _17 (.D(w17), .Q(r17), .clk(clk), .clr(reset));  // open: en
  Register #(.width(32)) _21 (.D(w21), .Q(r21), .clk(clk), .clr(reset));  // open: en
  Register #(.width(32)) _25 (.D(w25), .Q(r25), .clk(clk), .clr(reset));  // open: en
  Register #(.width(32)) _29 (.D(w29), .Q(r29), .clk(clk), .clr(reset));  // open: en
  Register #(.width(32)) _2 (.D(w2), .Q(r2), .clk(clk), .clr(reset));  // open: en
  Register #(.width(32)) _6 (.D(w6), .Q(r6), .clk(clk), .clr(reset));  // open: en
  Register #(.width(32)) _10 (.D(w10), .Q(r10), .clk(clk), .clr(reset));  // open: en
  Register #(.width(32)) _14 (.D(w14), .Q(r14), .clk(clk), .clr(reset));  // open: en
  Register #(.width(32)) _18 (.D(w18), .Q(r18), .clk(clk), .clr(reset));  // open: en
  Register #(.width(32)) _22 (.D(w22), .Q(r22), .clk(clk), .clr(reset));  // open: en
  Register #(.width(32)) _26 (.D(w26), .Q(r26), .clk(clk), .clr(reset));  // open: en
  Register #(.width(32)) _30 (.D(w30), .Q(r30), .clk(clk), .clr(reset));  // open: en
  Register #(.width(32)) _3 (.D(w3), .Q(r3), .clk(clk), .clr(reset));  // open: en
  Register #(.width(32)) _7 (.D(w7), .Q(r7), .clk(clk), .clr(reset));  // open: en
  Register #(.width(32)) _11 (.D(w11), .Q(r11), .clk(clk), .clr(reset));  // open: en
  Register #(.width(32)) _15 (.D(w15), .Q(r15), .clk(clk), .clr(reset));  // open: en
  Register #(.width(32)) _19 (.D(w19), .Q(r19), .clk(clk), .clr(reset));  // open: en
  Register #(.width(32)) _23 (.D(w23), .Q(r23), .clk(clk), .clr(reset));  // open: en
  Register #(.width(32)) _27 (.D(w27), .Q(r27), .clk(clk), .clr(reset));  // open: en
  Register #(.width(32)) _31 (.D(w31), .Q(r31), .clk(clk), .clr(reset));  // open: en
  Multiplexer #(.select(5), .width(32), .enable("false")) multiplexer_1 (
    .in0(r0), .in1(r1), .in2(r2), .in3(r3), .in4(r4), .in5(r5), .in6(r6), .in7(r7), .in8(r8), .in9(r9),
    .in10(r10), .in11(r11), .in12(r12), .in13(r13), .in14(r14), .in15(r15), .in16(r16), .in17(r17),
    .in18(r18), .in19(r19), .in20(r20), .in21(r21), .in22(r22), .in23(r23), .in24(r24), .in25(r25),
    .in26(r26), .in27(r27), .in28(r28), .in29(r29), .in30(r30), .in31(r31), .out(RD1), .sel(A1));
  Multiplexer #(.select(5), .width(32), .enable("false")) multiplexer_2 (
    .in0(r0), .in1(r1), .in2(r2), .in3(r3), .in4(r4), .in5(r5), .in6(r6), .in7(r7), .in8(r8), .in9(r9),
    .in10(r10), .in11(r11), .in12(r12), .in13(r13), .in14(r14), .in15(r15), .in16(r16), .in17(r17),
    .in18(r18), .in19(r19), .in20(r20), .in21(r21), .in22(r22), .in23(r23), .in24(r24), .in25(r25),
    .in26(r26), .in27(r27), .in28(r28), .in29(r29), .in30(r30), .in31(r31), .out(RD2), .sel(A2));

  // Other names for the same wires on the sheet: c = clk; r = reset
endmodule

module ALU (
  input  [3:0] ALUOp,
  input  [31:0] A,
  input  [31:0] B,
  output Zero,
  output [31:0] Result
);

  wire [31:0] \n32位减法器_1_result , \n32位加法器_1_result , \n32位或运算器_1_result ;

  \_32位加法器  \u_32位加法器_1  (.A(A), .B(B), .Result(\n32位加法器_1_result ));
  \_32位减法器  \u_32位减法器_1  (.A(A), .B(B), .Result(\n32位减法器_1_result ));
  \_32位或运算器  \u_32位或运算器_1  (.A(A), .B(B), .Result(\n32位或运算器_1_result ));
  Multiplexer #(.select(4), .width(32), .enable("false")) multiplexer_1 (
    .in0(\n32位加法器_1_result ), .in1(\n32位减法器_1_result ), .in2(\n32位或运算器_1_result ), .out(Result), .sel(ALUOp));  // open: in3, in4, in5, in6, in7, in8, in9, in10, in11, in12, in13, in14, in15
  Comparator #(.width(32), .mode("unsigned")) comparator_1 (.a(A), .b(B), .eq(Zero));  // open: gt, lt
endmodule

module DM (
  input  Clk,
  input  WE,
  input  [4:0] A,
  input  [31:0] WD,
  output [31:0] RD
);

  RAM #(.addrWidth(5), .dataWidth(32), .bus("separate")) ram_1 (
    .addr(A), .din(WD), .data(RD), .str(WE), .clk(Clk));  // open: sel, ld, clr
endmodule

module EXT (
  input  [1:0] EXTOp,
  input  [15:0] Imm,
  output [31:0] SI
);

  wire [31:0] bit_extender_1_out, bit_extender_2_out, bit_extender_3_out, shifter_1_out;

  assign bit_extender_1_out = {{16{Imm[15]}}, Imm};  // Bit_Extender bit_extender_1
  assign bit_extender_2_out = {{16{1'b0}}, Imm};  // Bit_Extender bit_extender_2
  assign bit_extender_3_out = {{16{Imm[15]}}, Imm};  // Bit_Extender bit_extender_3
  Shifter #(.width(32)) shifter_1 (.in(bit_extender_3_out), .\dist (5'b00010), .out(shifter_1_out));
  Multiplexer #(.select(2), .width(32), .enable("false")) multiplexer_1 (
    .in0(bit_extender_1_out), .in1(bit_extender_2_out), .in2({Imm, {16{1'b0}}}), .in3(shifter_1_out),
    .out(SI), .sel(EXTOp));
endmodule

module Controller (
  input  [5:0] Op,
  input  [5:0] Func,
  output RegDst,
  output RegWrite,
  output ALSrc,
  output MemWrite,
  output MemtoReg,
  output Branch,
  output [1:0] ExtOp,
  output [3:0] ALUControl
);

  wire and_logic1_1_addu, and_logic1_1_beq, and_logic1_1_lui, and_logic1_1_lw, and_logic1_1_ori,
       and_logic1_1_subu, and_logic1_1_sw, and_logic2_1_addu, and_logic2_1_beq, and_logic2_1_lui,
       and_logic2_1_lw, and_logic2_1_ori, and_logic2_1_subu, and_logic2_1_sw;

  AND_logic1 and_logic1_1 (
    .Op(Op), .addu(and_logic1_1_addu), .subu(and_logic1_1_subu), .ori(and_logic1_1_ori),
    .lw(and_logic1_1_lw), .sw(and_logic1_1_sw), .beq(and_logic1_1_beq), .lui(and_logic1_1_lui));
  OR_logic or_logic_1 (
    .addu(and_logic1_1_addu), .subu(and_logic1_1_subu), .ori(and_logic1_1_ori), .lw(and_logic1_1_lw),
    .sw(and_logic1_1_sw), .beq(and_logic1_1_beq), .lui(and_logic1_1_lui), .in_2(and_logic2_1_addu),
    .in_4(and_logic2_1_subu), .in_6(and_logic2_1_ori), .in_8(and_logic2_1_lw), .in_10(and_logic2_1_sw),
    .in_12(and_logic2_1_beq), .in_14(and_logic2_1_lui), .RegDst(RegDst), .RegWrite(RegWrite), .ALUSrc(ALSrc),
    .MemWrite(MemWrite), .MemtoReg(MemtoReg), .Branch(Branch), .ExtOp_0(ExtOp[0]), .ExtOp_1(ExtOp[1]),
    .ALUControl_0(ALUControl[0]), .ALUControl_1(ALUControl[1]), .ALUControl_0_2(ALUControl[2]),
    .ALUControl_1_2(ALUControl[3]));
  AND_logic2 and_logic2_1 (
    .addu(and_logic2_1_addu), .subu(and_logic2_1_subu), .ori(and_logic2_1_ori), .lw(and_logic2_1_lw),
    .sw(and_logic2_1_sw), .beq(and_logic2_1_beq), .lui(and_logic2_1_lui), .F(Func));
endmodule

module \_32位加法器  (
  input  [31:0] A,
  input  [31:0] B,
  output [31:0] Result
);

  Adder #(.width(32)) adder_1 (.a(A), .b(B), .out(Result));  // open: cin, cout
endmodule

module \_32位减法器  (
  input  [31:0] A,
  input  [31:0] B,
  output [31:0] Result
);

  Subtractor #(.width(32)) subtractor_1 (.a(A), .b(B), .out(Result));  // open: bin, bout
endmodule

module \_32位或运算器  (
  input  [31:0] A,
  input  [31:0] B,
  output [31:0] Result
);

  assign Result = A | B;  // OR_Gate or_1, 32 bits wide
endmodule

module AND_logic1 (
  input  [5:0] Op,
  output addu,
  output subu,
  output ori,
  output lw,
  output sw,
  output beq,
  output lui
);

  wire not_1_out, not_2_out, not_3_out, not_4_out, not_5_out, not_6_out;

  not not_1 (not_1_out, Op[5]);
  not not_2 (not_2_out, Op[3]);
  not not_3 (not_3_out, Op[4]);
  not not_4 (not_4_out, Op[1]);
  not not_5 (not_5_out, Op[2]);
  not not_6 (not_6_out, Op[0]);
  and u_addu (addu, not_6_out, not_4_out, not_5_out, not_5_out, not_3_out, not_1_out);
  and u_subu (subu, not_6_out, not_4_out, not_5_out, not_2_out, not_3_out, not_1_out);
  and u_ori (ori, Op[0], not_4_out, Op[2], Op[3], not_3_out, not_1_out);
  and u_lw (lw, Op[0], Op[1], not_5_out, not_2_out, not_3_out, Op[5]);
  and u_sw (sw, Op[0], Op[1], not_5_out, Op[3], not_3_out, Op[5]);
  and u_beq (beq, not_6_out, not_4_out, Op[2], not_2_out, not_3_out, not_1_out);
  and u_lui (lui, Op[0], Op[1], Op[2], Op[3], not_3_out, not_1_out);
endmodule

module AND_logic2 (
  input  [5:0] F,
  output addu,
  output subu,
  output ori,
  output lw,
  output sw,
  output beq,
  output lui
);

  wire not_1_out, not_2_out, not_3_out, not_4_out, not_5_out, not_6_out;

  and u_addu (addu, F[0], not_2_out, not_4_out, not_3_out, not_5_out, F[5]);
  and u_subu (subu, F[0], F[1], not_4_out, not_3_out, not_5_out, F[5]);
  not not_1 (not_1_out, F[0]);
  not not_2 (not_2_out, F[1]);
  not not_3 (not_3_out, F[3]);
  not not_4 (not_4_out, F[2]);
  not not_5 (not_5_out, F[4]);
  not not_6 (not_6_out, F[5]);

  assign beq = 1'b1;
  assign lui = 1'b1;
  assign lw = 1'b1;
  assign ori = 1'b1;
  assign sw = 1'b1;
endmodule

module OR_logic (
  input  addu,
  input  in_2,
  input  subu,
  input  in_4,
  input  ori,
  input  in_6,
  input  lw,
  input  in_8,
  input  sw,
  input  in_10,
  input  beq,
  input  in_12,
  input  lui,
  input  in_14,
  output RegDst,
  output RegWrite,
  output ALUSrc,
  output MemWrite,
  output MemtoReg,
  output Branch,
  output ExtOp_0,
  output ExtOp_1,
  output ALUControl_0,
  output ALUControl_1,
  output ALUControl_0_2,
  output ALUControl_1_2
);

  wire addu_out, beq_out, lui_out, lw_out, ori_out, subu_out, sw_out;

  and u_addu (addu_out, addu, in_2);
  and u_subu (subu_out, subu, in_4);
  and u_ori (ori_out, ori, in_6);
  and u_lw (lw_out, lw, in_8);
  and u_sw (sw_out, sw, in_10);
  and u_beq (beq_out, beq, in_12);
  and u_lui (lui_out, lui, in_14);
  or u_RegDst (RegDst, addu_out, subu_out);
  or u_RegWrite (RegWrite, addu_out, subu_out, ori_out, lw_out, lui_out);
  or u_ALUSrc (ALUSrc, ori_out, lw_out, sw_out, lui_out, 1'b0);
  or u_MemWrite (MemWrite, sw_out, 1'b0);
  or u_MemtoReg (MemtoReg, lw_out, 1'b0);
  or u_Branch (Branch, beq_out, 1'b0);
  or u_ExtOp_0 (ExtOp_0, ori_out, 1'b0);
  or u_ExtOp_1 (ExtOp_1, lui_out, 1'b0);
  or u_ALUControl_0 (ALUControl_0, subu_out, beq_out);
  or u_ALUControl_1 (ALUControl_1, ori_out, 1'b0);
  or ALUControl_2 (ALUControl_0_2, 1'b0, 1'b0);
  or ALUControl_3 (ALUControl_1_2, 1'b0, 1'b0);

  // Other names for the same wires on the sheet: addu_t = in_2; beq_t = in_12; lui_t = in_14; lw_t = in_8;
  //   ori_t = in_6; subu_t = in_4; sw_t = in_10
endmodule

module _1 (
);

  wire ALSrc, alu_1_zero, ALUSrc, Branch, Clk, MemtoReg, MemWrite, PCSrc, RegDst, RegWrite, Reset;
  wire [1:0] ExtOp;
  wire [3:0] ALUControl;
  wire [4:0] multiplexer_2_out;
  wire [29:0] adder_1_out, adder_2_out, bit_extender_1_out, ifu_1_pc, multiplexer_1_out;
  wire [31:0] alu_1_result, dm_1_rd, ext_1_si, grf_1_rd1, grf_1_rd2, ifu_1_instr, multiplexer_3_out,
       multiplexer_4_out;

  Multiplexer #(.width(30), .enable("false")) multiplexer_1 (
    .in0(adder_2_out), .in1(adder_1_out), .out(multiplexer_1_out), .sel(PCSrc));
  IFU ifu_1 (.Instr(ifu_1_instr), .Clk(Clk), .Reset(Reset), .PC_prime(multiplexer_1_out), .PC(ifu_1_pc));
  Adder #(.width(30)) adder_1 (.a(ifu_1_pc), .b(30'h1), .out(adder_1_out));  // open: cin, cout
  Multiplexer #(.width(5), .enable("false")) multiplexer_2 (
    .in0(ifu_1_instr[20:16]), .in1(ifu_1_instr[15:11]), .out(multiplexer_2_out), .sel(RegDst));
  Controller controller_1 (
    .Op(ifu_1_instr[31:26]), .Func(ifu_1_instr[5:0]), .RegDst(RegDst), .RegWrite(RegWrite), .ALSrc(ALUSrc),
    .MemWrite(MemWrite), .MemtoReg(MemtoReg), .Branch(Branch), .ExtOp(ExtOp), .ALUControl(ALUControl));
  GRF grf_1 (
    .A1(ifu_1_instr[25:21]), .A2(ifu_1_instr[20:16]), .A3(multiplexer_2_out), .WD(multiplexer_4_out),
    .RD1(grf_1_rd1), .RD2(grf_1_rd2), .clk(Clk), .WE(RegWrite), .reset(Reset));
  EXT ext_1 (.Imm(ifu_1_instr[15:0]), .SI(ext_1_si), .EXTOp(ExtOp));
  Multiplexer #(.width(32), .enable("false")) multiplexer_3 (
    .in0(grf_1_rd2), .in1(ext_1_si), .out(multiplexer_3_out), .sel(ALSrc));
  Bit_Extender #(.in_width(32), .out_width(30)) bit_extender_1 (.in(ext_1_si), .out(bit_extender_1_out));
  ALU alu_1 (.A(grf_1_rd1), .B(multiplexer_3_out), .Zero(alu_1_zero), .Result(alu_1_result), .ALUOp(ALUControl));
  Adder #(.width(30)) adder_2 (.a(bit_extender_1_out), .b(adder_1_out), .out(adder_2_out));  // open: cin, cout
  and and_1 (PCSrc, Branch, alu_1_zero);
  DM dm_1 (.A(alu_1_result[4:0]), .WD(grf_1_rd2), .RD(dm_1_rd), .Clk(Clk), .WE(MemWrite));
  Multiplexer #(.width(32), .enable("false")) multiplexer_4 (
    .in0(alu_1_result), .in1(dm_1_rd), .out(multiplexer_4_out), .sel(MemtoReg));
  // Pins of 2 and 4 bits meet at ALUControl
  // Pins of 5 and 32 bits meet at alu_1_result

  // Notes on the sheet:
  //   PCPlus
endmodule
