// Logisim project project3new.circ as structural Verilog: 11 circuits, main circuit GRF
module main (
  input  Reset,
  output [31:0] out_2,
  output out_3,
  output [4:0] out_4,
  output [31:0] out_5,
  output out_6,
  output [4:0] out_7,
  output [31:0] out_8
);

  wire alu_1_zero, ALUSrc, Branch, Clk, Jal, Jalr, Jr, Jump, MemtoReg, PCSrc, RegDst;
  wire [1:0] ExtOp;
  wire [3:0] ALUControl;
  wire [4:0] multiplexer_4_out;
  wire [31:0] adder_2_out, alu_1_result, dm_1_rd, ext_1_si, ifu_1_pc, Jraddress, multiplexer_1_out,
       multiplexer_2_out, multiplexer_3_out, multiplexer_6_out, multiplexer_7_out, PCPlus, shifter_1_out;

  Multiplexer #(.width(32), .enable("false")) multiplexer_1 (
    .in0(PCPlus), .in1(adder_2_out), .out(multiplexer_1_out), .sel(PCSrc));
  Clock clock_1 (.out(Clk));
  Multiplexer #(.width(32), .enable("false")) multiplexer_2 (
    .in0(multiplexer_1_out), .in1({PCPlus[31:28], out_2[25:0], 2'b00}), .out(multiplexer_2_out), .sel(Jump));
  Multiplexer #(.width(32), .enable("false")) multiplexer_3 (
    .in0(multiplexer_2_out), .in1(Jraddress), .out(multiplexer_3_out), .sel(Jr));
  IFU ifu_1 (.Instr(out_2), .Clk(Clk), .Reset(Reset), .PC_prime(multiplexer_3_out), .PC(ifu_1_pc));
  Controller controller_1 (
    .Op(out_2[31:26]), .Func(out_2[5:0]), .Jr(Jr), .Jalr(Jalr), .Jal(Jal), .Jump(Jump), .RegDst(RegDst),
    .RegWrite(out_3), .ALSrc(ALUSrc), .MemWrite(out_6), .MemtoReg(MemtoReg), .Branch(Branch), .ExtOp(ExtOp),
    .ALUControl(ALUControl));
  Adder #(.width(32)) adder_1 (.a(ifu_1_pc), .b(32'h4), .out(PCPlus));  // open: cin, cout
  Multiplexer #(.width(5), .enable("false")) multiplexer_4 (
    .in0(out_2[20:16]), .in1(out_2[15:11]), .out(multiplexer_4_out), .sel(RegDst));
  GRF grf_1 (
    .A1(out_2[25:21]), .A2(out_2[20:16]), .A3(out_4), .WD(out_5), .RD1(Jraddress), .RD2(out_8), .clk(Clk),
    .WE(out_3), .reset(Reset));
  Multiplexer #(.width(5), .enable("false")) multiplexer_5 (
    .in0(multiplexer_4_out), .in1({5{1'b1}}), .out(out_4), .sel(Jal));
  EXT ext_1 (.Imm(out_2[15:0]), .SI(ext_1_si), .EXTOp(ExtOp));
  Multiplexer #(.width(32), .enable("false")) multiplexer_6 (
    .in0(out_8), .in1(ext_1_si), .out(multiplexer_6_out), .sel(ALUSrc));
  Shifter #(.width(32)) shifter_1 (.in(ext_1_si), .\dist (5'b00010), .out(shifter_1_out));
  ALU alu_1 (
    .A(Jraddress), .B(multiplexer_6_out), .Zero(alu_1_zero),
    .Result({alu_1_result[31:7], out_7, alu_1_result[1:0]}), .ALUOp(ALUControl));
  Adder #(.width(32)) adder_2 (.a(shifter_1_out), .b(PCPlus), .out(adder_2_out));  // open: cin, cout
  and and_1 (PCSrc, Branch, alu_1_zero);
  DM dm_1 (.A(out_7), .WD(out_8), .RD(dm_1_rd), .Clk(Clk), .WE(out_6));
  Multiplexer #(.width(32), .enable("false")) multiplexer_7 (
    .in0({alu_1_result[31:7], out_7, alu_1_result[1:0]}), .in1(dm_1_rd), .out(multiplexer_7_out),
    .sel(MemtoReg));
  Multiplexer #(.width(32), .enable("false")) multiplexer_8 (
    .in0(multiplexer_7_out), .in1(PCPlus), .out(out_5), .sel(Jal));

  // Other names for the same wires on the sheet: MemAddr[4:0] = out_7; Instr[31:0] = out_2; MemData[31:0] = out_8;
  //   MemWrite = out_6; RegAddr[4:0] = out_4; RegData[31:0] = out_5; RegWrite = out_3

  // Notes on the sheet:
  //   PCPlus
endmodule

module IFU (
  input  [31:0] PC_prime,
  input  Clk,
  input  Reset,
  output [31:0] Instr,
  output [31:0] PC
);

  Register #(.width(32)) u_PC (.D(PC_prime), .Q(PC), .clk(Clk), .clr(Reset));  // open: en
  ROM #(.addrWidth(5), .dataWidth(32)) rom_1 (.addr(PC[6:2]), .data(Instr));  // open: sel

  // Notes on the sheet:
  //   contents of rom_1 (hex, n*v repeats v):
  //   34080000 34090001 34100001 34110004 34120028 11120004 ad090000 1304821 1114021 8000c05 34080000
  //   34090000 34100000 11120004 8d090000 2098021 1114021 8000c0d ad100000 3c014489 34287253
endmodule

module GRF (
  input  clk,
  input  WE,
  input  [4:0] A1,
  input  [4:0] A2,
  input  [4:0] A3,
  input  [31:0] WD,
  input  reset,
  output [31:0] RD1,
  output [31:0] RD2
);

  wire [31:0] r0, r1, r2, r3, r4, r5, r6, r7, r8, r9, r10, r11, r12, r13, r14, r15, r16, r17, r18, r19, r20,
       r21, r22, r23, r24, r25, r26, r27, r28, r29, r30, r31, w0, w1, w2, w3, w4, w5, w6, w7, w8, w9, w10,
       w11, w12, w13, w14, w15, w16, w17, w18, w19, w20, w21, w22, w23, w24, w25, w26, w27, w28, w29, w30,
       w31;

  Demultiplexer #(.select(5), .width(32), .tristate("true")) demultiplexer_1 (
    .out0(w0), .out1(w1), .out2(w2), .out3(w3), .out4(w4), .out5(w5), .out6(w6), .out7(w7), .out8(w8),
    .out9(w9), .out10(w10), .out11(w11), .out12(w12), .out13(w13), .out14(w14), .out15(w15), .out16(w16),
    .out17(w17), .out18(w18), .out19(w19), .out20(w20), .out21(w21), .out22(w22), .out23(w23), .out24(w24),
    .out25(w25), .out26(w26), .out27(w27), .out28(w28), .out29(w29), .out30(w30), .out31(w31), .in(WD),
    .sel(A3), .en(WE));
  Register #(.width(32)) _0 (.D({32{1'b0}}), .Q(r0), .clk(clk), .clr(reset));  // open: en
  Register #(.width(32)) _4 (.D(w4), .Q(r4), .clk(clk), .clr(reset));  // open: en
  Register #(.width(32)) _8 (.D(w8), .Q(r8), .clk(clk), .clr(reset));  // open: en
  Register #(.width(32)) _12 (.D(w12), .Q(r12), .clk(clk), .clr(reset));  // open: en
  Register #(.width(32)) _16 (.D(w16), .Q(r16), .clk(clk), .clr(reset));  // open: en
  Register #(.width(32)) _20 (.D(w20), .Q(r20), .clk(clk), .clr(reset));  // open: en
  Register #(.width(32)) _24 (.D(w24), .Q(r24), .clk(clk), .clr(reset));  // open: en
  Register #(.width(32)) _28 (.D(w28), .Q(r28), .clk(clk), .clr(reset));  // open: en
  Register #(.width(32)) _1 (.D(w1), .Q(r1), .clk(clk), .clr(reset));  // open: en
  Register #(.width(32)) _5 (.D(w5), .Q(r5), .clk(clk), .clr(reset));  // open: en
  Register #(.width(32)) _9 (.D(w9), .Q(r9), .clk(clk), .clr(reset));  // open: en
  Register #(.width(32)) _13 (.D(w13), .Q(r13), .clk(clk), .clr(reset));  // open: en
  Register #(.width(32)) _17 (.D(w17), .Q(r17), .clk(clk), .clr(reset));  // open: en
  Register #(.width(32)) _21 (.D(w21), .Q(r21), .clk(clk), .clr(reset));  // open: en
  Register #(.width(32)) _25 (.D(w25), .Q(r25), .clk(clk), .clr(reset));  // open: en
  Register #(.width(32)) _29 (.D(w29), .Q(r29), .clk(clk), .clr(reset));  // open: en
  Register #(.width(32)) _2 (.D(w2), .Q(r2), .clk(clk), .clr(reset));  // open: en
  Register #(.width(32)) _6 (.D(w6), .Q(r6), .clk(clk), .clr(reset));  // open: en
  Register #(.width(32)) _10 (.D(w10), .Q(r10), .clk(clk), .clr(reset));  // open: en
  Register #(.width(32)) _14 (.D(w14), .Q(r14), .clk(clk), .clr(reset));  // open: en
  Register #(.width(32)) _18 (.D(w18), .Q(r18), .clk(clk), .clr(reset));  // open: en
  Register #(.width(32)) _22 (.D(w22), .Q(r22), .clk(clk), .clr(reset));  // open: en
  Register #(.width(32)) _26 (.D(w26), .Q(r26), .clk(clk), .clr(reset));  // open: en
  Register #(.width(32)) _30 (.D(w30), .Q(r30), .clk(clk), .clr(reset));  // open: en
  Register #(.width(32)) _3 (.D(w3), .Q(r3), .clk(clk), .clr(reset));  // open: en
  Register #(.width(32)) _7 (.D(w7), .Q(r7), .clk(clk), .clr(reset));  // open: en
  Register #(.width(32)) _11 (.D(w11), .Q(r11), .clk(clk), .clr(reset));  // open: en
  Register #(.width(32)) _15 (.D(w15), .Q(r15), .clk(clk), .clr(reset));  // open: en
  Register #(.width(32)) _19 (.D(w19), .Q(r19), .clk(clk), .clr(reset));  // open: en
  Register #(.width(32)) _23 (.D(w23), .Q(r23), .clk(clk), .clr(reset));  // open: en
  Register #(.width(32)) _27 (.D(w27), .Q(r27), .clk(clk), .clr(reset));  // open: en
  Register #(.width(32)) _31 (.D(w31), .Q(r31), .clk(clk), .clr(reset));  // open: en
  Multiplexer #(.select(5), .width(32), .enable("false")) multiplexer_1 (
    .in0(r0), .in1(r1), .in2(r2), .in3(r3), .in4(r4), .in5(r5), .in6(r6), .in7(r7), .in8(r8), .in9(r9),
    .in10(r10), .in11(r11), .in12(r12), .in13(r13), .in14(r14), .in15(r15), .in16(r16), .in17(r17),
    .in18(r18), .in19(r19), .in20(r20), .in21(r21), .in22(r22), .in23(r23), .in24(r24), .in25(r25),
    .in26(r26), .in27(r27), .in28(r28), .in29(r29), .in30(r30), .in31(r31), .out(RD1), .sel(A1));
  Multiplexer #(.select(5), .width(32), .enable("false")) multiplexer_2 (
    .in0(r0), .in1(r1), .in2(r2), .in3(r3), .in4(r4), .in5(r5), .in6(r6), .in7(r7), .in8(r8), .in9(r9),
    .in10(r10), .in11(r11), .in12(r12), .in13(r13), .in14(r14), .in15(r15), .in16(r16), .in17(r17),
    .in18(r18), .in19(r19), .in20(r20), .in21(r21), .in22(r22), .in23(r23), .in24(r24), .in25(r25),
    .in26(r26), .in27(r27), .in28(r28), .in29(r29), .in30(r30), .in31(r31), .out(RD2), .sel(A2));

  // Other names for the same wires on the sheet: c = clk; r = reset
endmodule

module ALU (
  input  [3:0] ALUOp,
  input  [31:0] A,
  input  [31:0] B,
  output Zero,
  output [31:0] Result
);

  wire [31:0] adder_1_out, or_1_out, subtractor_1_out, \溢出判断_1_overflow ;

  Adder #(.width(32)) adder_1 (.a(A), .b(B), .out(adder_1_out));  // open: cin, cout
  Subtractor #(.width(32)) subtractor_1 (.a(A), .b(B), .out(subtractor_1_out));  // open: bin, bout
  assign or_1_out = A | B;  // OR_Gate or_1, 32 bits wide
  \溢出判断  \u_溢出判断_1  (.A(A), .B(B), .Overflow(\溢出判断_1_overflow ));
  Multiplexer #(.select(4), .width(32), .enable("false")) multiplexer_1 (
    .in0(adder_1_out), .in1(subtractor_1_out), .in2(or_1_out), .in3(\溢出判断_1_overflow ), .out(Result),
    .sel(ALUOp));  // open: in4, in5, in6, in7, in8, in9, in10, in11, in12, in13, in14, in15
  Comparator #(.width(32), .mode("unsigned")) comparator_1 (.a(A), .b(B), .eq(Zero));  // open: gt, lt
endmodule

module DM (
  input  Clk,
  input  WE,
  input  [4:0] A,
  input  [31:0] WD,
  output [31:0] RD
);

  RAM #(.addrWidth(5), .dataWidth(32), .bus("separate")) ram_1 (
    .addr(A), .din(WD), .data(RD), .str(WE), .clk(Clk));  // open: sel, ld, clr
endmodule

module EXT (
  input  [1:0] EXTOp,
  input  [15:0] Imm,
  output [31:0] SI
);

  wire [31:0] bit_extender_1_out, bit_extender_2_out, bit_extender_3_out, shifter_1_out;

  assign bit_extender_1_out = {{16{Imm[15]}}, Imm};  // Bit_Extender bit_extender_1
  assign bit_extender_2_out = {{16{1'b0}}, Imm};  // Bit_Extender bit_extender_2
  assign bit_extender_3_out = {{16{Imm[15]}}, Imm};  // Bit_Extender bit_extender_3
  Shifter #(.width(32)) shifter_1 (.in(bit_extender_3_out), .\dist (5'b00010), .out(shifter_1_out));
  Multiplexer #(.select(2), .width(32), .enable("false")) multiplexer_1 (
    .in0(bit_extender_1_out), .in1(bit_extender_2_out), .in2({Imm, {16{1'b0}}}), .in3(shifter_1_out),
    .out(SI), .sel(EXTOp));
endmodule

module Controller (
  input  [5:0] Op,
  input  [5:0] Func,
  output Jr,
  output Jalr,
  output Jal,
  output Jump,
  output RegDst,
  output RegWrite,
  output ALSrc,
  output MemWrite,
  output MemtoReg,
  output Branch,
  output [1:0] ExtOp,
  output [3:0] ALUControl
);

  wire and_logic1_1_addu, and_logic1_1_beq, and_logic1_1_j, and_logic1_1_jal, and_logic1_1_jalr,
       and_logic1_1_jr, and_logic1_1_lui, and_logic1_1_lw, and_logic1_1_ori, and_logic1_1_sao,
       and_logic1_1_subu, and_logic1_1_sw, and_logic2_1_addu, and_logic2_1_beq, and_logic2_1_j,
       and_logic2_1_jal, and_logic2_1_jalr, and_logic2_1_jr, and_logic2_1_lui, and_logic2_1_lw,
       and_logic2_1_ori, and_logic2_1_sao, and_logic2_1_subu, and_logic2_1_sw;

  AND_logic1 and_logic1_1 (
    .Op(Op), .addu(and_logic1_1_addu), .subu(and_logic1_1_subu), .ori(and_logic1_1_ori),
    .lw(and_logic1_1_lw), .sw(and_logic1_1_sw), .beq(and_logic1_1_beq), .lui(and_logic1_1_lui),
    .j(and_logic1_1_j), .jal(and_logic1_1_jal), .jalr(and_logic1_1_jalr), .jr(and_logic1_1_jr),
    .sao(and_logic1_1_sao));
  OR_logic or_logic_1 (
    .addu(and_logic1_1_addu), .subu(and_logic1_1_subu), .ori(and_logic1_1_ori), .lw(and_logic1_1_lw),
    .sw(and_logic1_1_sw), .beq(and_logic1_1_beq), .lui(and_logic1_1_lui), .j(and_logic1_1_j),
    .jal(and_logic1_1_jal), .jalr(and_logic1_1_jalr), .jr(and_logic1_1_jr), .sao(and_logic1_1_sao),
    .Jr_3(Jr), .Jalr_3(Jalr), .Jal_3(Jal), .Jump(Jump), .RegDst(RegDst), .RegWrite(RegWrite), .ALUSrc(ALSrc),
    .MemWrite(MemWrite), .MemtoReg(MemtoReg), .Branch(Branch), .ExtOp_0(ExtOp[0]), .ExtOp_1(ExtOp[1]),
    .ALUControl_0(ALUControl[0]), .ALUControl_1(ALUControl[1]), .ALUControl_0_2(ALUControl[2]),
    .ALUControl_1_2(ALUControl[3]), .addu_2(and_logic2_1_addu), .subu_2(and_logic2_1_subu),
    .ori_2(and_logic2_1_ori), .lw_2(and_logic2_1_lw), .sw_2(and_logic2_1_sw), .beq_2(and_logic2_1_beq),
    .lui_2(and_logic2_1_lui), .j_2(and_logic2_1_j), .jal_2(and_logic2_1_jal), .jalr_2(and_logic2_1_jalr),
    .jr_2(and_logic2_1_jr), .sao_2(and_logic2_1_sao));
  AND_logic2 and_logic2_1 (
    .addu(and_logic2_1_addu), .subu(and_logic2_1_subu), .ori(and_logic2_1_ori), .lw(and_logic2_1_lw),
    .sw(and_logic2_1_sw), .beq(and_logic2_1_beq), .lui(and_logic2_1_lui), .j(and_logic2_1_j),
    .jal(and_logic2_1_jal), .jalr(and_logic2_1_jalr), .jr(and_logic2_1_jr), .sao(and_logic2_1_sao), .F(Func));
endmodule

module AND_logic1 (
  input  [5:0] Op,
  output addu,
  output subu,
  output ori,
  output lw,
  output sw,
  output beq,
  output lui,
  output j,
  output jal,
  output jalr,
  output jr,
  output sao
);

  wire not_1_out, not_2_out, not_3_out, not_4_out, not_5_out, not_6_out;

  not not_1 (not_1_out, Op[5]);
  not not_2 (not_2_out, Op[4]);
  not not_3 (not_3_out, Op[3]);
  not not_4 (not_4_out, Op[1]);
  not not_5 (not_5_out, Op[2]);
  not not_6 (not_6_out, Op[0]);
  and u_addu (addu, not_6_out, not_4_out, not_5_out, not_5_out, not_2_out, not_1_out);
  and u_subu (subu, not_6_out, not_4_out, not_5_out, not_3_out, not_2_out, not_1_out);
  and u_ori (ori, Op[0], not_4_out, Op[2], Op[3], not_2_out, not_1_out);
  and u_lw (lw, Op[0], Op[1], not_5_out, not_3_out, not_2_out, Op[5]);
  and u_sw (sw, Op[0], Op[1], not_5_out, Op[3], not_2_out, Op[5]);
  and u_beq (beq, not_6_out, not_4_out, Op[2], not_3_out, not_2_out, not_1_out);
  and u_lui (lui, Op[0], Op[1], Op[2], Op[3], not_2_out, not_1_out);
  and u_j (j, not_6_out, Op[1], not_5_out, not_3_out, not_2_out, not_1_out);
  and u_jal (jal, Op[0], Op[1], not_5_out, not_3_out, not_2_out, not_1_out);
  and u_jalr (jalr, not_6_out, not_4_out, not_5_out, not_3_out, not_2_out, not_1_out);
  and u_jr (jr, not_6_out, not_4_out, not_5_out, not_3_out, not_2_out, not_1_out);
  and jr_2 (sao, not_6_out, not_4_out, not_5_out, not_3_out, not_2_out, not_1_out);
endmodule

module AND_logic2 (
  input  [5:0] F,
  output addu,
  output subu,
  output ori,
  output lw,
  output sw,
  output beq,
  output lui,
  output j,
  output jal,
  output jalr,
  output jr,
  output sao
);

  wire not_1_out, not_2_out, not_3_out, not_4_out, not_5_out, not_6_out;

  and u_addu (addu, F[0], not_1_out, not_3_out, not_4_out, not_5_out, F[5]);
  and u_subu (subu, F[0], F[1], not_3_out, not_4_out, not_5_out, F[5]);
  and u_jalr (jalr, F[0], not_1_out, not_3_out, F[3], not_5_out, not_6_out);
  and u_jr (jr, not_2_out, not_1_out, not_3_out, F[3], not_5_out, not_6_out);
  and u_sao (sao, F[0], F[1], F[2], F[3], F[4], not_6_out);
  not not_1 (not_1_out, F[1]);
  not not_2 (not_2_out, F[0]);
  not not_3 (not_3_out, F[2]);
  not not_4 (not_4_out, F[3]);
  not not_5 (not_5_out, F[4]);
  not not_6 (not_6_out, F[5]);

  assign beq = 1'b1;
  assign j = 1'b1;
  assign jal = 1'b1;
  assign lui = 1'b1;
  assign lw = 1'b1;
  assign ori = 1'b1;
  assign sw = 1'b1;
endmodule

module OR_logic (
  input  addu,
  input  addu_2,
  input  subu,
  input  subu_2,
  input  ori,
  input  ori_2,
  input  lw,
  input  lw_2,
  input  sw,
  input  sw_2,
  input  beq,
  input  beq_2,
  input  lui,
  input  lui_2,
  input  j,
  input  j_2,
  input  jal,
  input  jal_2,
  input  jalr,
  input  jalr_2,
  input  jr,
  input  jr_2,
  input  sao,
  input  sao_2,
  output Jr_3,
  output Jalr_3,
  output Jal_3,
  output Jump,
  output RegDst,
  output RegWrite,
  output ALUSrc,
  output MemWrite,
  output MemtoReg,
  output Branch,
  output ExtOp_0,
  output ExtOp_1,
  output ALUControl_0,
  output ALUControl_1,
  output ALUControl_0_2,
  output ALUControl_1_2
);

  wire addu_out, beq_out, j_out, jal_out, jalr_out, jr_out, lui_out, lw_out, ori_out, sao_out, subu_out,
       sw_out;

  and u_addu (addu_out, addu, addu_2);
  and u_subu (subu_out, subu, subu_2);
  and u_ori (ori_out, ori, ori_2);
  and u_lw (lw_out, lw, lw_2);
  and u_sw (sw_out, sw, sw_2);
  and u_beq (beq_out, beq, beq_2);
  and u_lui (lui_out, lui, lui_2);
  and u_j (j_out, j, j_2);
  and u_jal (jal_out, jal, jal_2);
  and u_jalr (jalr_out, jalr, jalr_2);
  and u_jr (jr_out, jr, jr_2);
  and u_sao (sao_out, sao, sao_2);
  or u_Jr_2 (Jr_3, jr_out, jal_out);
  buf u_Jalr_2 (Jalr_3, 1'b0);  // OR_Gate
  buf u_Jal_2 (Jal_3, jal_out);  // OR_Gate
  or u_Jump (Jump, j_out, jal_out, jr_out);
  or u_RegDst (RegDst, addu_out, subu_out, sao_out);
  or u_RegWrite (RegWrite, addu_out, subu_out, ori_out, lw_out, lui_out, sao_out);
  or u_ALUSrc (ALUSrc, ori_out, lw_out, sw_out, lui_out);
  buf u_MemWrite (MemWrite, sw_out);  // OR_Gate
  buf u_MemtoReg (MemtoReg, lw_out);  // OR_Gate
  or u_Branch (Branch, beq_out, j_out);
  buf u_ExtOp_0 (ExtOp_0, ori_out);  // OR_Gate
  buf u_ExtOp_1 (ExtOp_1, lui_out);  // OR_Gate
  or u_ALUControl_0 (ALUControl_0, subu_out, beq_out, sao_out);
  or u_ALUControl_1 (ALUControl_1, ori_out, sao_out);
  buf ALUControl_2 (ALUControl_0_2, 1'b0);  // OR_Gate
  buf ALUControl_3 (ALUControl_1_2, 1'b0);  // OR_Gate

  // Other names for the same wires on the sheet: addu_t = addu_2; beq_t = beq_2; j_t = j_2; jal_t = jal_2;
  //   jalr_t = jalr_2; jr_t = jr_2; lui_t = lui_2; lw_t = lw_2; ori_t = ori_2; sao_t = sao_2; subu_t = subu_2;
  //   sw_t = sw_2
endmodule

module \溢出判断  (
  input  [31:0] A,
  input  [31:0] B,
  output [31:0] Overflow
);

  wire adder_1_cout, adder_2_cout, comparator_1_eq, not_1_out;
  wire [31:0] adder_1_out;

  Adder #(.width(32)) adder_1 (.a(A), .b(B), .out(adder_1_out), .cout(adder_1_cout));  // open: cin
  Adder #(.width(1)) adder_2 (.a(A[31]), .b(A[31]), .cin(adder_1_cout), .cout(adder_2_cout));  // open: out
  Comparator #(.width(1), .mode("unsigned")) comparator_1 (
    .a(adder_1_out[31]), .b(adder_2_cout), .eq(comparator_1_eq));  // open: gt, lt
  not not_1 (not_1_out, comparator_1_eq);
  assign Overflow = {{31{1'b0}}, not_1_out};  // Bit_Extender bit_extender_1
endmodule
